# Fritzing sketch bulbuino (saved by Fritzing 0.3.15b)
breadboards: 1

parts:
  Arduino1 = Arduino
  IC1 = IC, DIP package, 6 pins [chip_label=4N35 spacing=300mil]
  J1 = female pin header, 1 pin [form="♀ (female)"]
  J2 = female pin header, 1 pin [form="♀ (female)"]
  LED1 = Red LED - 5mm
  LED1_2 = Red LED - 5mm
  LED1_3 = Red LED - 5mm
  LED1_4 = Red LED - 5mm
  LED1_5 = Red LED - 5mm
  LED1_6 = Red LED - 5mm
  LED1_7 = Red LED - 5mm
  LED1_8 = Red LED - 5mm
  R1 = Resistor [resistance=220 package=THT]
  R1_2 = Resistor [resistance=220 package=THT]
  R1_3 = Resistor [resistance=220 package=THT]
  R1_4 = Resistor [resistance=220 package=THT]
  R1_5 = Resistor [resistance=220 package=THT]
  R1_6 = Resistor [resistance=220 package=THT]
  R1_7 = Resistor [resistance=220 package=THT]
  R1_8 = Resistor [resistance=220 package=THT]
  J2_2 = female pin header, 1 pin [form="♀ (female)"]
  R1_9 = Resistor [resistance=220 package=THT]
  IC1_2 = IC, DIP package, 6 pins [chip_label=4N35 spacing=300mil]
  S1 = Pushbutton [package="[THT]"]
  S2 = Pushbutton [package="[THT]"]
  S3 = Pushbutton [package="[THT]"]
  R2 = Resistor [resistance=10k package=THT]
  R3 = Resistor [resistance=330k package=THT]
  R2_2 = Resistor [resistance=5k package=THT]

nets:
  N1: Arduino1.GND, IC1.pin2, R1.Pin_1, R1_2.Pin_1, R1_3.Pin_1, R1_4.Pin_1, R1_5.Pin_1, R1_6.Pin_1, R1_7.Pin_1, R1_8.Pin_1, IC1_2.pin2, S1.Pin_3, S1.Pin_4, S2.Pin_3, S2.Pin_4, R2_2.Pin_1
  N2: Arduino1.D12, R1_9.Pin_1
  N3: Arduino1.D11, S1.Pin_1, S1.Pin_2
  N4: Arduino1.D10, S2.Pin_1, S2.Pin_2
  N5: Arduino1.D9, LED1_8.anode
  N6: Arduino1.D8, LED1_7.anode
  N7: Arduino1.D7, LED1_6.anode
  N8: Arduino1.D6, LED1_5.anode
  N9: Arduino1.D5, LED1_4.anode
  N10: Arduino1.D4, LED1_3.anode
  N11: Arduino1.D3, LED1_2.anode
  N12: Arduino1.D2, LED1.anode
  N13: Arduino1.A0, S3.Pin_3, S3.Pin_4, R3.Pin_1, R2_2.Pin_0
  N14: IC1.pin1, R1_9.Pin_0, IC1_2.pin1
  N15: IC1.pin4, J2.pin1, IC1_2.pin4
  N16: IC1.pin5, J2_2.pin1
  N17: J1.pin1, IC1_2.pin5
  N18: LED1.cathode, R1.Pin_0
  N19: LED1_2.cathode, R1_2.Pin_0
  N20: LED1_3.cathode, R1_3.Pin_0
  N21: LED1_4.cathode, R1_4.Pin_0
  N22: LED1_5.cathode, R1_5.Pin_0
  N23: LED1_6.cathode, R1_6.Pin_0
  N24: LED1_7.cathode, R1_7.Pin_0
  N25: LED1_8.cathode, R1_8.Pin_0
  N26: S3.Pin_1, S3.Pin_2, R2.Pin_0

notes:
  Camera
  Red = GND
